# Fritzing sketch Project_H (saved by Fritzing 0.9.3b)
breadboards: 1

parts:
  Part1 = Arduino Uno (Rev3)
  IC1 = L293D [package=THT]
  LED1 = LED - 5mm [color="Red (633nm)" package="5 mm [THT]"]
  LED2 = LED - 5mm [color="Green (570nm)" package="5 mm [THT]"]
  Passive_Buzzer = Piezo Speaker
  R1 = Resistor [tolerance=±5% resistance=220 package="2512 [SMD]"]
  VCC1 = Battery block 9V
  VCC2 = Battery block 9V
  R3 = Resistor [tolerance=±5% resistance=220 package="2512 [SMD]"]
  M2 = DC Motor
  R4 = Resistor [tolerance=±5% resistance=10k package="2512 [SMD]"]
  U2 = LCD-16X2 [package=lcd-8x2-kit]
  DHT11 = Humidity and Temperature Sensor RHT03

nets:
  N1: Part1.D8, U2.E
  N2: Part1.D9_PWM, U2.DB4
  N3: Part1.D10_PWM/SS, U2.DB5
  N4: Part1.D11_PWM/MOSI, U2.DB6
  N5: Part1.D12/MISO, U2.DB7
  N6: Part1.D13/SCK, Passive_Buzzer.pin1
  N7: Part1.D2, DHT11.Data-signal
  N8: Part1.D3_PWM, LED1.anode
  N9: Part1.D4, IC1.In_1
  N10: Part1.D5_PWM, IC1.Enable_1
  N11: Part1.D6_PWM, IC1.In_2
  N12: Part1.D7, U2.RS
  5V: Part1.5V, LED2.anode, VCC2.+, U2.VDD, DHT11.Vcc
  GND: Part1.GND, Passive_Buzzer.pin2, R1.Pin_0, VCC2.-, R3.Pin_0, R4.Pin_1, U2.VSS, U2.R_W, DHT11.GND_1
  N13: IC1.Out_1_(_Controlled_by_Enable_1_), M2.pin_2
  N14: IC1.0V, VCC1.-
  N15: IC1.Out_2_(_Controlled_by_Enable_1_), M2.pin_1
  N16: IC1.+Vmotor, VCC1.+
  N17: LED1.cathode, R1.Pin_1
  N18: LED2.cathode, R3.Pin_1
  N19: R4.Pin_0, U2.VO
